# Fritzing sketch topraknem (saved by Fritzing 0.9.3b)
breadboards: 1

parts:
  Parça1 = Arduino Uno (Rev3)
  J1 = Piezo Speaker
  R1 = Resistor [tolerance=±5% resistance=330 package=THT]
  Parça2 = Soil Moisture Sensor

nets:
  N1: Parça1.D8, Parça2.SIG
  GND: Parça1.GND, R1.Pin_1, Parça2.GND
  5V: Parça1.5V, J1.pin2, Parça2.VCC
  N2: J1.pin1, R1.Pin_0
